// Logisim project real_alu.circ as structural Verilog: 17 circuits, main circuit Union
module Union (
  input  [7:0] in_1,
  input  in_2,
  input  in_3,
  input  in_4,
  input  in_5,
  input  [7:0] in_6,
  output [7:0] out_7
);

  wire [7:0] arithmetic_unit_1_out_7, logic_unit_1_aluout;

  Logic_Unit logic_unit_1 (
    .inA(in_1), .Sel2(in_3), .Sel1(in_4), .Sel0(in_5), .aluOut(logic_unit_1_aluout));  // open: inB, OF
  assign out_7 = logic_unit_1_aluout | arithmetic_unit_1_out_7;  // OR_Gate or_1, 8 bits wide
  Arithmetic_Unit arithmetic_unit_1 (
    .in_3(in_3), .in_4(in_4), .in_5(in_5), .inB(in_6), .out_7(arithmetic_unit_1_out_7), .in_2(in_2));  // open: inA
endmodule

module Logic_Unit (
  input  [7:0] inA,
  input  Sel2,
  input  Sel1,
  input  Sel0,
  input  [7:0] inB,
  output [7:0] aluOut,
  output OF
);

  wire dxshiftinb_1_of, logicdecoder_1_out_4, logicdecoder_1_out_5, logicdecoder_1_out_6,
       logicdecoder_1_out_7, logicdecoder_1_out_8, sxshiftinb_1_of;
  wire [7:0] dxshiftinb_1_aluout, ina_inb_1_aluout, inaorinb_1_aluout, notinb_1_aluout, sxshiftinb_1_aluout;

  inA_inB ina_inb_1 (.inA(inA), .in_2(logicdecoder_1_out_4), .inB(inB), .aluOut(ina_inb_1_aluout));
  inAorinB inaorinb_1 (.in_3(logicdecoder_1_out_5), .inA(inA), .inB(inB), .aluOut(inaorinb_1_aluout));
  LogicDecoder logicdecoder_1 (
    .out_4(logicdecoder_1_out_4), .out_5(logicdecoder_1_out_5), .out_6(logicdecoder_1_out_6),
    .out_7(logicdecoder_1_out_7), .out_8(logicdecoder_1_out_8), .Sel2(Sel2), .Sel1(Sel1), .Sel0(Sel0));
  NotinB notinb_1 (.in_2(logicdecoder_1_out_6), .inB(inB), .aluout(notinb_1_aluout));
  assign aluOut = ina_inb_1_aluout | inaorinb_1_aluout | notinb_1_aluout | sxshiftinb_1_aluout | dxshiftinb_1_aluout;  // OR_Gate or_1, 8 bits wide
  SxShiftinB sxshiftinb_1 (.inB(inB), .in_2(logicdecoder_1_out_7), .OF(sxshiftinb_1_of), .aluOut(sxshiftinb_1_aluout));
  DxshiftinB dxshiftinb_1 (.inB(inB), .OF(dxshiftinb_1_of), .aluOut(dxshiftinb_1_aluout), .in_2(logicdecoder_1_out_8));
  or or_2 (OF, sxshiftinb_1_of, dxshiftinb_1_of);
endmodule

module Arithmetic_Unit (
  input  [7:0] inA,
  input  in_2,
  input  in_3,
  input  in_4,
  input  in_5,
  input  [7:0] inB,
  output [7:0] out_7
);

  wire arithmeticdecoder_1_out_5, arithmeticdecoder_1_out_6, arithmeticdecoder_1_out_7,
       arithmeticdecoder_1_out_8, arithmeticdecoder_1_out_9;
  wire [7:0] and_1_out, bit_extender_1_out, decrementer_inb_1_out_18, ina_add_inb_1_out_5,
       ina_sub_inb_1_out_5, incrementer_inb_1_out_18;

  Decrementer_inB decrementer_inb_1 (
    .in_1(inB[7]), .in_2(inB[6]), .in_3(inB[5]), .in_4(inB[4]), .E(arithmeticdecoder_1_out_8), .in_5(inB[3]),
    .in_6(inB[2]), .in_7(inB[1]), .in_8(inB[0]), .out_11(decrementer_inb_1_out_18[7]),
    .out_12(decrementer_inb_1_out_18[6]), .out_13(decrementer_inb_1_out_18[5]),
    .out_14(decrementer_inb_1_out_18[4]), .out_15(decrementer_inb_1_out_18[3]),
    .out_16(decrementer_inb_1_out_18[2]), .out_17(decrementer_inb_1_out_18[1]),
    .out_18(decrementer_inb_1_out_18[0]));  // open: out_10
  assign bit_extender_1_out = {{7{arithmeticdecoder_1_out_9}}, arithmeticdecoder_1_out_9};  // Bit_Extender bit_extender_1
  assign and_1_out = bit_extender_1_out & inA;  // AND_Gate and_1, 8 bits wide
  Incrementer_inB incrementer_inb_1 (
    .in_1(inB[7]), .in_2(inB[6]), .in_3(inB[5]), .in_4(inB[4]), .in_5(inB[3]), .in_6(inB[2]), .in_7(inB[1]),
    .in_8(inB[0]), .out_11(incrementer_inb_1_out_18[7]), .out_12(incrementer_inb_1_out_18[6]),
    .out_13(incrementer_inb_1_out_18[5]), .out_14(incrementer_inb_1_out_18[4]),
    .out_15(incrementer_inb_1_out_18[3]), .out_16(incrementer_inb_1_out_18[2]),
    .out_17(incrementer_inb_1_out_18[1]), .out_18(incrementer_inb_1_out_18[0]), .E(arithmeticdecoder_1_out_7));  // open: out_10
  assign out_7 = and_1_out | decrementer_inb_1_out_18 | incrementer_inb_1_out_18 | ina_sub_inb_1_out_5 | ina_add_inb_1_out_5;  // OR_Gate or_1, 8 bits wide
  ArithmeticDecoder arithmeticdecoder_1 (
    .out_5(arithmeticdecoder_1_out_5), .out_6(arithmeticdecoder_1_out_6), .out_7(arithmeticdecoder_1_out_7),
    .out_8(arithmeticdecoder_1_out_8), .out_9(arithmeticdecoder_1_out_9), .Sel3(in_2), .Sel2(in_3),
    .I1(in_4), .I0(in_5));
  inA_sub_inB ina_sub_inb_1 (
    .in_2(arithmeticdecoder_1_out_6), .in_1(inA), .in_3(inB), .out_5(ina_sub_inb_1_out_5));  // open: out_4
  inA_add_inB ina_add_inb_1 (
    .in_1(inA), .in_2(inB), .E(arithmeticdecoder_1_out_5), .out_5(ina_add_inb_1_out_5));  // open: out_4
endmodule

module inA_inB (
  input  [7:0] inA,
  input  in_2,
  input  [7:0] inB,
  output [7:0] aluOut
);

  wire [7:0] bit_extender_1_out;

  assign bit_extender_1_out = {{7{in_2}}, in_2};  // Bit_Extender bit_extender_1
  assign aluOut = inA & bit_extender_1_out & inB;  // AND_Gate and_1, 8 bits wide
endmodule

module inAorinB (
  input  [7:0] inA,
  input  [7:0] inB,
  input  in_3,
  output [7:0] aluOut
);

  wire [7:0] bit_extender_1_out, or_1_out;

  assign bit_extender_1_out = {{7{in_3}}, in_3};  // Bit_Extender bit_extender_1
  assign or_1_out = inA | inB;  // OR_Gate or_1, 8 bits wide
  assign aluOut = bit_extender_1_out & or_1_out;  // AND_Gate and_1, 8 bits wide
endmodule

module NotinB (
  input  [7:0] inB,
  input  in_2,
  output [7:0] aluout
);

  wire [7:0] bit_extender_1_out, not_1_out;

  assign bit_extender_1_out = {{7{in_2}}, in_2};  // Bit_Extender bit_extender_1
  assign not_1_out = ~inB;  // NOT_Gate not_1, 8 bits wide
  assign aluout = bit_extender_1_out & not_1_out;  // AND_Gate and_1, 8 bits wide
endmodule

module SxShiftinB (
  input  [7:0] inB,
  input  in_2,
  output OF,
  output [7:0] aluOut
);

  wire [6:0] bit_extender_1_out;

  and and_1 (OF, in_2, inB[7]);
  assign aluOut[7:1] = inB[6:0] & bit_extender_1_out;  // AND_Gate and_2, 7 bits wide
  assign bit_extender_1_out = {{6{in_2}}, in_2};  // Bit_Extender bit_extender_1

  assign aluOut[0] = 1'b0;
endmodule

module DxshiftinB (
  input  [7:0] inB,
  input  in_2,
  output OF,
  output [7:0] aluOut
);

  wire [6:0] bit_extender_1_out;

  assign bit_extender_1_out = {{6{in_2}}, in_2};  // Bit_Extender bit_extender_1
  and and_1 (OF, in_2, inB[0]);
  assign aluOut[6:0] = inB[7:1] & bit_extender_1_out;  // AND_Gate and_2, 7 bits wide

  assign aluOut[7] = 1'b0;
endmodule

module LogicDecoder (
  input  Sel2,
  input  Sel1,
  input  Sel0,
  output out_4,
  output out_5,
  output out_6,
  output out_7,
  output out_8
);

  wire not_1_out, not_2_out, not_3_out;

  not not_1 (not_1_out, Sel2);
  not not_2 (not_2_out, Sel0);
  not not_3 (not_3_out, Sel1);
  and and_1 (out_4, not_1_out, not_3_out, not_2_out);
  and and_2 (out_5, not_1_out, not_3_out, Sel0);
  and and_3 (out_6, not_1_out, Sel1, not_2_out);
  and and_4 (out_7, not_1_out, Sel1, Sel0);
  and and_5 (out_8, Sel2, not_3_out, not_2_out);
endmodule

module Incrementer_inB (
  input  in_1,
  input  in_2,
  input  in_3,
  input  in_4,
  input  in_5,
  input  in_6,
  input  in_7,
  input  in_8,
  input  E,
  output out_10,
  output out_11,
  output out_12,
  output out_13,
  output out_14,
  output out_15,
  output out_16,
  output out_17,
  output out_18
);

  wire fulladder_1_s, fulladder_2_cout, fulladder_2_s, fulladder_3_cout, fulladder_3_s, fulladder_4_cout,
       fulladder_4_s, fulladder_5_cout, fulladder_5_s, fulladder_6_cout, fulladder_6_s, fulladder_7_cout,
       fulladder_7_s, fulladder_8_cout, fulladder_8_s;

  and and_1 (out_11, E, fulladder_1_s);
  FullAdder fulladder_1 (.Cout(out_10), .S(fulladder_1_s), .A(1'b0), .B(in_1), .Cin(fulladder_2_cout));
  and and_2 (out_12, E, fulladder_2_s);
  FullAdder fulladder_2 (.Cout(fulladder_2_cout), .S(fulladder_2_s), .A(1'b0), .B(in_2), .Cin(fulladder_3_cout));
  and and_3 (out_13, E, fulladder_3_s);
  FullAdder fulladder_3 (.Cout(fulladder_3_cout), .S(fulladder_3_s), .A(1'b0), .B(in_3), .Cin(fulladder_4_cout));
  and and_4 (out_14, E, fulladder_4_s);
  FullAdder fulladder_4 (.Cout(fulladder_4_cout), .S(fulladder_4_s), .A(1'b0), .B(in_4), .Cin(fulladder_5_cout));
  and and_5 (out_15, E, fulladder_5_s);
  FullAdder fulladder_5 (.Cout(fulladder_5_cout), .S(fulladder_5_s), .A(1'b0), .B(in_5), .Cin(fulladder_6_cout));
  and and_6 (out_16, E, fulladder_6_s);
  FullAdder fulladder_6 (.Cout(fulladder_6_cout), .S(fulladder_6_s), .A(1'b0), .B(in_6), .Cin(fulladder_7_cout));
  FullAdder fulladder_7 (.Cout(fulladder_7_cout), .S(fulladder_7_s), .A(1'b0), .B(in_7), .Cin(fulladder_8_cout));
  and and_7 (out_17, E, fulladder_7_s);
  and and_8 (out_18, E, fulladder_8_s);
  FullAdder fulladder_8 (.Cout(fulladder_8_cout), .S(fulladder_8_s), .A(1'b1), .B(in_8), .Cin(1'b0));
endmodule

module HalfAdder (
  input  A,
  input  B,
  output S,
  output C
);

  xor xor_1 (S, A, B);
  and and_1 (C, A, B);
endmodule

module FullAdder (
  input  A,
  input  B,
  input  Cin,
  output Cout,
  output S
);

  wire halfadder_1_c, halfadder_2_c, halfadder_2_s;

  or or_1 (Cout, halfadder_2_c, halfadder_1_c);
  HalfAdder halfadder_1 (.A(halfadder_2_s), .B(Cin), .S(S), .C(halfadder_1_c));
  HalfAdder halfadder_2 (.A(A), .B(B), .S(halfadder_2_s), .C(halfadder_2_c));
endmodule

module Decrementer_inB (
  input  in_1,
  input  in_2,
  input  in_3,
  input  in_4,
  input  in_5,
  input  in_6,
  input  in_7,
  input  in_8,
  input  E,
  output out_10,
  output out_11,
  output out_12,
  output out_13,
  output out_14,
  output out_15,
  output out_16,
  output out_17,
  output out_18
);

  wire fulladder_1_s, fulladder_2_cout, fulladder_2_s, fulladder_3_cout, fulladder_3_s, fulladder_4_cout,
       fulladder_4_s, fulladder_5_cout, fulladder_5_s, fulladder_6_cout, fulladder_6_s, fulladder_7_cout,
       fulladder_7_s, fulladder_8_cout, fulladder_8_s;

  and and_1 (out_11, E, fulladder_1_s);
  FullAdder fulladder_1 (.Cout(out_10), .S(fulladder_1_s), .A(1'b1), .B(in_1), .Cin(fulladder_2_cout));
  and and_2 (out_12, E, fulladder_2_s);
  FullAdder fulladder_2 (.Cout(fulladder_2_cout), .S(fulladder_2_s), .A(1'b1), .B(in_2), .Cin(fulladder_3_cout));
  FullAdder fulladder_3 (.Cout(fulladder_3_cout), .S(fulladder_3_s), .A(1'b1), .B(in_3), .Cin(fulladder_4_cout));
  and and_3 (out_13, E, fulladder_3_s);
  and and_4 (out_14, E, fulladder_4_s);
  FullAdder fulladder_4 (.Cout(fulladder_4_cout), .S(fulladder_4_s), .A(1'b1), .B(in_4), .Cin(fulladder_5_cout));
  and and_5 (out_15, E, fulladder_5_s);
  FullAdder fulladder_5 (.Cout(fulladder_5_cout), .S(fulladder_5_s), .A(1'b1), .B(in_5), .Cin(fulladder_6_cout));
  and and_6 (out_16, E, fulladder_6_s);
  FullAdder fulladder_6 (.Cout(fulladder_6_cout), .S(fulladder_6_s), .A(1'b1), .B(in_6), .Cin(fulladder_7_cout));
  and and_7 (out_17, E, fulladder_7_s);
  FullAdder fulladder_7 (.Cout(fulladder_7_cout), .S(fulladder_7_s), .A(1'b1), .B(in_7), .Cin(fulladder_8_cout));
  and and_8 (out_18, E, fulladder_8_s);
  FullAdder fulladder_8 (.Cout(fulladder_8_cout), .S(fulladder_8_s), .A(1'b0), .B(in_8), .Cin(E));
endmodule

module inA_add_inB (
  input  [7:0] in_1,
  input  [7:0] in_2,
  input  E,
  output out_4,
  output [7:0] out_5
);

  wire fulladder_2_cout, fulladder_3_cout, fulladder_4_cout, fulladder_5_cout, fulladder_6_cout,
       fulladder_7_cout, fulladder_8_cout;
  wire [7:0] bit_extender_1_out, fulladder_8_s;

  FullAdder fulladder_1 (.Cout(out_4), .S(fulladder_8_s[7]), .A(in_1[7]), .B(in_2[7]), .Cin(fulladder_2_cout));
  FullAdder fulladder_2 (
    .Cout(fulladder_2_cout), .S(fulladder_8_s[6]), .A(in_1[6]), .B(in_2[6]), .Cin(fulladder_3_cout));
  FullAdder fulladder_3 (
    .Cout(fulladder_3_cout), .S(fulladder_8_s[5]), .A(in_1[5]), .B(in_2[5]), .Cin(fulladder_4_cout));
  FullAdder fulladder_4 (
    .Cout(fulladder_4_cout), .S(fulladder_8_s[4]), .A(in_1[4]), .B(in_2[4]), .Cin(fulladder_5_cout));
  assign out_5 = fulladder_8_s & bit_extender_1_out;  // AND_Gate and_1, 8 bits wide
  FullAdder fulladder_5 (
    .Cout(fulladder_5_cout), .S(fulladder_8_s[3]), .A(in_1[3]), .B(in_2[3]), .Cin(fulladder_6_cout));
  FullAdder fulladder_6 (
    .Cout(fulladder_6_cout), .S(fulladder_8_s[2]), .A(in_1[2]), .B(in_2[2]), .Cin(fulladder_7_cout));
  FullAdder fulladder_7 (
    .Cout(fulladder_7_cout), .S(fulladder_8_s[1]), .A(in_1[1]), .B(in_2[1]), .Cin(fulladder_8_cout));
  FullAdder fulladder_8 (.Cout(fulladder_8_cout), .S(fulladder_8_s[0]), .A(in_1[0]), .B(in_2[0]), .Cin(1'b0));
  assign bit_extender_1_out = {{7{E}}, E};  // Bit_Extender bit_extender_1
endmodule

module inA_sub_inB (
  input  [7:0] in_1,
  input  in_2,
  input  [7:0] in_3,
  output out_4,
  output [7:0] out_5
);

  wire adderforsub_1_out_4;
  wire [7:0] adderforsub_1_out_5, bit_extender_1_out, not_2_out;

  not not_1 (out_4, adderforsub_1_out_4);
  assign not_2_out = ~in_3;  // NOT_Gate not_2, 8 bits wide
  assign out_5 = adderforsub_1_out_5 & bit_extender_1_out;  // AND_Gate and_1, 8 bits wide
  Adderforsub adderforsub_1 (
    .out_4(adderforsub_1_out_4), .E(in_2), .in_1(in_1), .in_2(not_2_out), .out_5(adderforsub_1_out_5));
  assign bit_extender_1_out = {{7{in_2}}, in_2};  // Bit_Extender bit_extender_1
endmodule

module ArithmeticDecoder (
  input  Sel3,
  input  Sel2,
  input  I1,
  input  I0,
  output out_5,
  output out_6,
  output out_7,
  output out_8,
  output out_9
);

  wire not_2_out, not_3_out, not_4_out;

  // NOT_Gate not_1 has open pins: in=Sel3, out=open
  not not_2 (not_2_out, Sel2);
  not not_3 (not_3_out, I1);
  not not_4 (not_4_out, I0);
  and and_1 (out_5, Sel2, not_3_out, I0);
  and and_2 (out_6, Sel2, I1, not_4_out);
  and and_3 (out_7, I0, I1, Sel2);
  and and_4 (out_8, Sel3, not_2_out, not_3_out, not_4_out);
  and and_5 (out_9, Sel3, not_2_out, not_3_out, I0);
endmodule

module Adderforsub (
  input  [7:0] in_1,
  input  [7:0] in_2,
  input  E,
  output out_4,
  output [7:0] out_5
);

  wire fulladder_2_cout, fulladder_3_cout, fulladder_4_cout, fulladder_5_cout, fulladder_6_cout,
       fulladder_7_cout, fulladder_8_cout;
  wire [7:0] bit_extender_1_out, fulladder_8_s;

  FullAdder fulladder_1 (.Cout(out_4), .S(fulladder_8_s[7]), .A(in_1[7]), .B(in_2[7]), .Cin(fulladder_2_cout));
  FullAdder fulladder_2 (
    .Cout(fulladder_2_cout), .S(fulladder_8_s[6]), .A(in_1[6]), .B(in_2[6]), .Cin(fulladder_3_cout));
  FullAdder fulladder_3 (
    .Cout(fulladder_3_cout), .S(fulladder_8_s[5]), .A(in_1[5]), .B(in_2[5]), .Cin(fulladder_4_cout));
  FullAdder fulladder_4 (
    .Cout(fulladder_4_cout), .S(fulladder_8_s[4]), .A(in_1[4]), .B(in_2[4]), .Cin(fulladder_5_cout));
  assign out_5 = fulladder_8_s & bit_extender_1_out;  // AND_Gate and_1, 8 bits wide
  FullAdder fulladder_5 (
    .Cout(fulladder_5_cout), .S(fulladder_8_s[3]), .A(in_1[3]), .B(in_2[3]), .Cin(fulladder_6_cout));
  FullAdder fulladder_6 (
    .Cout(fulladder_6_cout), .S(fulladder_8_s[2]), .A(in_1[2]), .B(in_2[2]), .Cin(fulladder_7_cout));
  FullAdder fulladder_7 (
    .Cout(fulladder_7_cout), .S(fulladder_8_s[1]), .A(in_1[1]), .B(in_2[1]), .Cin(fulladder_8_cout));
  FullAdder fulladder_8 (.Cout(fulladder_8_cout), .S(fulladder_8_s[0]), .A(in_1[0]), .B(in_2[0]), .Cin(E));
  assign bit_extender_1_out = {{7{E}}, E};  // Bit_Extender bit_extender_1
endmodule
